# Fritzing sketch schema (saved by Fritzing 0.9.2b)
breadboards: 1

parts:
  OLED1 = 128x64 Monochrom OLED Display with SPI Control
  Part1 = Arduino Yun
  S1 = Pushbutton [package="[SMD]"]
  S2 = Pushbutton [package="[SMD]"]
  R3 = Rotary Potentiometer (Large) [maximum_resistance=100kΩ package=THT]
  U1 = POT [package=pot_alpha_rv16af-20]

nets:
  N1: OLED1.Data, Part1.D9_PWM
  N2: OLED1.Clock, Part1.D10_PWM/SS
  N3: OLED1.SA0/DC, Part1.D11_PWM/MOSI
  N4: OLED1.Reset, Part1.D13/SCK
  N5: OLED1.CS, Part1.D12/MISO
  3V3: OLED1.3v3, OLED1.Vin, Part1.5V, S1.Pin_1, S1.Pin_2, S2.Pin_3, S2.Pin_4, R3.leg2, U1.E
  GND: OLED1.GND, Part1.GND, Part1.D4, Part1.D5_PWM, S1.Pin_3, S1.Pin_4, S2.Pin_1, S2.Pin_2, R3.leg1, U1.A
  N6: Part1.A0, U1.S
  N7: Part1.A1, R3.wiper
